// Digital circuit latency_test.dig as structural Verilog
module latency_test (
);

  wire button_1_out, or_1_out, zenohsubscriber_1_p1;

  Button button_1 (.out(button_1_out));
  // ZenohSubscriber #(.zenohKeyExpr("latency_test/button")) zenohsubscriber_1: pin names not known; wires that end beside it: zenohsubscriber_1_p1
  or or_1 (or_1_out, button_1_out, zenohsubscriber_1_p1);
  // ZenohPublisher #(.zenohKeyExpr("latency_test/light")) zenohpublisher_1: pin names not known; wires that end beside it: or_1_out
endmodule
