// Digital circuit pub_circuit.dig as structural Verilog
module pub_circuit (
  input  clk
);

  // ZenohPublisher #(.zenohKeyExpr("test/pub1")) zenohpublisher_1: pin names not known; wires that end beside it: clk
endmodule
