// Digital circuit ram_circuit.dig as structural Verilog
module ram_circuit (
  input  clk
);

  wire zenohramdualaccess_1_p8, zenohsubscriber_1_p1, zenohsubscriber_2_p1, zenohsubscriber_3_p1,
       zenohsubscriber_4_p1, zenohsubscriber_5_p1, zenohsubscriber_6_p2, zenohsubscriber_7_p1,
       zenohsubscriber_8_p1, zenohsubscriber_9_p1, zenohsubscriber_10_p1, zenohsubscriber_11_p1;
  wire [6:0] zenohramdualport_1_p6;
  wire [31:0] zenohramdualaccess_1_p7;

  // ZenohSubscriber #(.zenohKeyExpr("ram1/clock")) zenohsubscriber_1: pin names not known; wires that end beside it: zenohsubscriber_1_p1
  // ZenohSubscriber #(.zenohKeyExpr("ram1/addr1"), .Bits(8)) zenohsubscriber_2: pin names not known; wires that end beside it: zenohsubscriber_2_p1
  // ZenohSubscriber #(.zenohKeyExpr("ram1/addr2"), .Bits(8)) zenohsubscriber_3: pin names not known; wires that end beside it: zenohsubscriber_3_p1
  // ZenohSubscriber #(.zenohKeyExpr("ram2/in_data"), .Bits(7)) zenohsubscriber_4: pin names not known; wires that end beside it: zenohsubscriber_4_p1
  // ZenohSubscriber #(.zenohKeyExpr("ram2/clock")) zenohsubscriber_5: pin names not known; wires that end beside it: zenohsubscriber_5_p1
  // ZenohSubscriber #(.zenohKeyExpr("ram1/str")) zenohsubscriber_6: pin names not known; wires that end beside it: clk, zenohsubscriber_6_p2
  // ZenohSubscriber #(.zenohKeyExpr("ram1/ld")) zenohsubscriber_7: pin names not known; wires that end beside it: zenohsubscriber_7_p1
  // ZenohSubscriber #(.zenohKeyExpr("ram1/in_d1"), .Bits(32)) zenohsubscriber_8: pin names not known; wires that end beside it: zenohsubscriber_8_p1
  // ZenohSubscriber #(.zenohKeyExpr("ram2/addr"), .Bits(4)) zenohsubscriber_9: pin names not known; wires that end beside it: zenohsubscriber_9_p1
  // ZenohSubscriber #(.zenohKeyExpr("ram2/str")) zenohsubscriber_10: pin names not known; wires that end beside it: zenohsubscriber_10_p1
  // ZenohSubscriber #(.zenohKeyExpr("ram2/ld")) zenohsubscriber_11: pin names not known; wires that end beside it: zenohsubscriber_11_p1
  // ZenohRAMDualAccess #(.AddrBits(8), .zenohKeyExpr("ram1/ram"), .Bits(32)) zenohramdualaccess_1: pin names not known; wires that end beside it: zenohsubscriber_6_p2, zenohsubscriber_1_p1, zenohsubscriber_7_p1, zenohsubscriber_2_p1, zenohsubscriber_8_p1, zenohsubscriber_3_p1, zenohramdualaccess_1_p7, zenohramdualaccess_1_p8
  // ZenohRAMDualPort #(.AddrBits(4), .zenohKeyExpr("ram2/ram"), .Bits(7)) zenohramdualport_1: pin names not known; wires that end beside it: zenohsubscriber_9_p1, zenohsubscriber_4_p1, zenohsubscriber_10_p1, zenohsubscriber_5_p1, zenohsubscriber_11_p1, zenohramdualport_1_p6
  PullDown #(.Bits(32)) pulldown_1 (.out(zenohramdualaccess_1_p7));
  PullDown #(.Bits(7)) pulldown_2 (.out(zenohramdualport_1_p6));
  // ZenohPublisher #(.zenohKeyExpr("ram1/out_d1"), .Bits(32)) zenohpublisher_1: pin names not known; wires that end beside it: zenohramdualaccess_1_p7
  // ZenohPublisher #(.zenohKeyExpr("ram1/out_d2"), .Bits(32)) zenohpublisher_2: pin names not known; wires that end beside it: zenohramdualaccess_1_p8
  // ZenohPublisher #(.zenohKeyExpr("ram2/out_data"), .Bits(7)) zenohpublisher_3: pin names not known; wires that end beside it: zenohramdualport_1_p6
endmodule
