// Digital circuit reg_circuit.dig as structural Verilog
module reg_circuit (
  input  clk
);

  wire zenohsubscriber_1_p1;
  wire [31:0] zenohregister_1_p1, zenohregister_1_p4;

  // ZenohSubscriber #(.zenohKeyExpr("test/enable")) zenohsubscriber_1: pin names not known; wires that end beside it: zenohsubscriber_1_p1
  // ZenohRegister #(.Bits(32), .zenohKeyExpr("test/reg")) zenohregister_1: pin names not known; wires that end beside it: zenohregister_1_p1, clk, zenohsubscriber_1_p1, zenohregister_1_p4
  Add #(.Bits(32)) add_1 (.a(zenohregister_1_p4), .b(32'h2), .c_i(1'b0), .s(zenohregister_1_p1));  // open: c_o

  // Notes on the sheet:
  //   clk: Hz: 100
endmodule
