// Digital circuit sub_circuit.dig as structural Verilog
module sub_circuit (
  input  clk
);

  wire zenohsubscriber_1_p1;
  wire [7:0] add_1_s, zenohsubscriber_2_p1;

  // ZenohSubscriber #(.zenohKeyExpr("test/sub1"), .Bits(8)) zenohsubscriber_1: pin names not known; wires that end beside it: zenohsubscriber_1_p1
  // ZenohSubscriber #(.zenohKeyExpr("test/sub2"), .Bits(8)) zenohsubscriber_2: pin names not known; wires that end beside it: zenohsubscriber_2_p1, clk
  Add #(.Bits(8)) add_1 (.a(zenohsubscriber_2_p1), .b(8'h5), .c_i(1'b0), .s(add_1_s));  // open: c_o
  // ZenohPublisher #(.zenohKeyExpr("test/pub1"), .Bits(8)) zenohpublisher_1: pin names not known; wires that end beside it: zenohsubscriber_1_p1
  // ZenohPublisher #(.zenohKeyExpr("test/pub2"), .Bits(8)) zenohpublisher_2: pin names not known; wires that end beside it: add_1_s
endmodule
