// Digital circuit subsync_circuit.dig as structural Verilog
module subsync_circuit (
  input  clk
);

  wire zenohsubscriber_1_p1;
  wire [15:0] zenohsyncsubscriber_1_p2;

  // ZenohSubscriber #(.zenohKeyExpr("test/clock")) zenohsubscriber_1: pin names not known; wires that end beside it: zenohsubscriber_1_p1
  // ZenohSyncSubscriber #(.Bits(16), .zenohKeyExpr("test/sub_sync")) zenohsyncsubscriber_1: pin names not known; wires that end beside it: zenohsubscriber_1_p1, zenohsyncsubscriber_1_p2
  // ZenohPublisher #(.Bits(16), .zenohKeyExpr("test/output")) zenohpublisher_1: pin names not known; wires that end beside it: clk, zenohsyncsubscriber_1_p2
  PullDown #(.Bits(16)) pulldown_1 (.out(zenohsyncsubscriber_1_p2));
endmodule
