// Digital circuit alu.dig as structural Verilog
module alu (
  input  [31:0] in_1,
  input  [31:0] in_2,
  input  [3:0] operation,
  output [31:0] out,
  output zero
);

  wire [0:0] comparator_1_lt, signed_lt;
  wire [31:0] add_1_s, and_1_out, barrelshifter_1_out, barrelshifter_2_out, barrelshifter_3_out, or_1_out,
       sub_1_s, xor_1_out;

  Add #(.Bits(32)) add_1 (.a(in_1), .b(in_2), .c_i(1'b0), .s(add_1_s));  // open: c_o
  Sub #(.Bits(32)) sub_1 (.a(in_1), .b(in_2), .c_i(1'b0), .s(sub_1_s));  // open: c_o
  BarrelShifter #(.Bits(32), .barrelShifterMode("arithmetic"), .direction("right")) barrelshifter_1 (
    .in(in_1), .shift(in_2[5:0]), .out(barrelshifter_1_out));
  BarrelShifter #(.Bits(32), .direction("right")) barrelshifter_2 (
    .in(in_1), .shift(in_2[5:0]), .out(barrelshifter_2_out));
  BarrelShifter #(.Bits(32)) barrelshifter_3 (.in(in_1), .shift(in_2[5:0]), .out(barrelshifter_3_out));
  assign and_1_out = in_1 & in_2;  // And and_1, 32 bits wide
  assign or_1_out = in_1 | in_2;  // Or or_1, 32 bits wide
  assign xor_1_out = in_1 ^ in_2;  // XOr xor_1, 32 bits wide
  Comparator #(.Signed("true"), .Bits(32)) \signed  (.a(in_1), .b(in_2), .lt(signed_lt[0]));  // open: gt, eq
  Comparator #(.Bits(32)) comparator_1 (.a(in_1), .b(in_2), .lt(comparator_1_lt[0]));  // open: gt, eq
  Multiplexer #(.Selector_Bits(4), .Bits(32)) multiplexer_1 (
    .sel(operation), .in_0(add_1_s), .in_1(sub_1_s), .in_2(barrelshifter_1_out), .in_3(barrelshifter_2_out),
    .in_4(barrelshifter_3_out), .in_5(32'h77777777), .in_6(and_1_out), .in_7(32'h77777777), .in_8(or_1_out),
    .in_9(32'h77777777), .in_10(xor_1_out), .in_11(32'h77777777), .in_12({{31{1'b0}}, signed_lt[0]}),
    .in_13({{31{1'b0}}, comparator_1_lt[0]}), .in_14(32'h77777777), .in_15(32'h77777777), .out(out));
  Comparator #(.Bits(32)) comparator_2 (.a(out), .b({32{1'b0}}), .eq(zero));  // open: gt, lt

  // Other names for the same wires on the sheet: shift[5:0] = in_2[5:0]
endmodule
