// Digital circuit alu_control.dig as structural Verilog
module alu_control (
  input  [2:0] funct3,
  input  i30,
  input  [1:0] ALUOp,
  output [3:0] Op
);

  wire and_1_out, and_2_out, and_3_out, and_4_out, and_5_out, and_6_out, and_7_out, and_8_out, and_9_out,
       and_10_out, not_1_out, not_2_out, not_3_out, not_4_out;

  not not_1 (not_1_out, funct3[2]);
  not not_2 (not_2_out, funct3[1]);
  not not_3 (not_3_out, funct3[0]);
  not not_4 (not_4_out, i30);
  and and_1 (and_1_out, ALUOp[1], funct3[1], not_1_out);
  and and_2 (and_2_out, ALUOp[1], not_3_out, funct3[2]);
  and and_3 (and_3_out, ALUOp[1], funct3[0], funct3[1], not_4_out);
  and and_4 (and_4_out, ALUOp[1], funct3[0], not_1_out);
  and and_5 (and_5_out, ALUOp[1], funct3[1], not_1_out);
  and and_6 (and_6_out, ALUOp[1], not_2_out, funct3[2]);
  and and_7 (and_7_out, ALUOp[1], funct3[0], funct3[2]);
  and and_8 (and_8_out, ALUOp[1], not_3_out, not_2_out, not_1_out, i30);
  and and_9 (and_9_out, ALUOp[1], funct3[0], not_2_out, funct3[2], not_4_out);
  and and_10 (and_10_out, ALUOp[1], funct3[0], funct3[1], not_1_out);
  or or_1 (Op[3], and_1_out, and_2_out);
  or or_2 (Op[2], and_3_out, and_4_out, and_5_out);
  or or_3 (Op[1], and_6_out, and_7_out);
  or or_4 (Op[0], and_8_out, and_9_out, and_10_out);

  // Notes on the sheet:
  //   funct3: funct3 part of instruction, part in determining alu operation
  //   Op: operation to use by ALU
  //   i30: bit of instruction usually used to tell between add/sub, left/right, etc
  //   ALUOp: alu op from control block
endmodule
