// Digital circuit control.dig as structural Verilog
module control (
  input  [6:0] opcode,
  output [1:0] ALUOp,
  output Jalr,
  output ALUSrc,
  output MemtoReg,
  output RegWrite,
  output MemRead,
  output MemWrite,
  output Branch,
  output PCToReg,
  output CondBranch,
  output UpperImm
);

  wire and_2_out, and_5_out, and_6_out, not_1_out, not_2_out, not_3_out, not_4_out, not_5_out;

  not not_1 (not_1_out, opcode[6]);
  not not_2 (not_2_out, opcode[5]);
  not not_3 (not_3_out, opcode[4]);
  not not_4 (not_4_out, opcode[3]);
  not not_5 (not_5_out, opcode[2]);
  and and_1 (Jalr, opcode[2], not_4_out);
  and and_2 (and_2_out, not_3_out, not_1_out);
  and and_3 (MemtoReg, not_3_out, not_2_out);
  or or_1 (RegWrite, opcode[2], opcode[4], not_2_out);
  and and_4 (MemWrite, not_5_out, not_3_out, opcode[5]);
  and and_5 (and_5_out, opcode[2], not_3_out, opcode[5], opcode[6]);
  and and_6 (and_6_out, not_4_out, not_3_out, opcode[5], opcode[6]);
  and and_7 (PCToReg, opcode[2], not_3_out, opcode[5], opcode[6]);
  and and_8 (CondBranch, not_5_out, not_4_out, not_3_out, opcode[5], opcode[6]);
  and and_9 (UpperImm, opcode[2], not_4_out, opcode[4], opcode[5], not_1_out);
  or or_2 (ALUSrc, opcode[2], and_2_out, not_2_out);
  or or_3 (Branch, and_5_out, and_6_out);

  assign ALUOp = {opcode[5], 1'b0};
  assign MemRead = 1'b1;

  // Notes on the sheet:
  //   opcode: 6-0 of the instruction
endmodule
