// Digital circuit cpu.dig as structural Verilog
module cpu (
  input  clk
);

  wire add_1_c_o, alu_1_zero, and_1_out, clk_t, control_1_alusrc, control_1_branch, control_1_condbranch,
       control_1_jalr, control_1_memread, control_1_memtoreg, control_1_memwrite, control_1_pctoreg,
       control_1_regwrite, control_1_upperimm, not_1_out, not_2_out, or_2_out, xor_1_out,
       zenohsubscriber_1_p1;
  wire [1:0] control_1_aluop;
  wire [2:0] funct3;
  wire [3:0] alu_control_1_op;
  wire [4:0] add_2_s, multiplexer_1_out, multiplexer_2_out, multiplexer_4_out, PC_p1, PC_p4;
  wire [6:2] add_1_s;
  wire [11:0] BTypeImmediate;
  wire [24:0] ins;
  wire [31:0] alu_1_out, bitextender_1_out, bitextender_2_out, multiplexer_5_out, multiplexer_6_out,
       multiplexer_7_out, multiplexer_8_out, multiplexer_9_out, ramdualport_1_d, register_file_1_data1_out,
       register_file_1_data2_out;

  // ZenohSubscriber #(.zenohKeyExpr("clock")) zenohsubscriber_1: pin names not known; wires that end beside it: zenohsubscriber_1_p1
  or or_1 (clk_t, clk, zenohsubscriber_1_p1);
  // ZenohRegister #(.zenohKeyExpr("pc"), .Bits(5), .isProgramCounter("true")) PC: pin names not known; wires that end beside it: PC_p1, clk_t, 1'b1, PC_p4
  ROM #(.AddrBits(5), .Bits(32)) rom_1 (
    .A(PC_p4), .sel(1'b1),
    .D({BTypeImmediate[11], BTypeImmediate[9:4], ins[24:15], funct3, BTypeImmediate[3:0], BTypeImmediate[10], ins[6:0]}));
  Add #(.Bits(5)) add_1 (.a(PC_p4), .b(5'b00001), .c_i(1'b0), .s(add_1_s), .c_o(add_1_c_o));
  // Probe on {BTypeImmediate[11], ins[19:15], funct3, ins[20], BTypeImmediate[9:4], ins[24:21], 1'b0}
  // Probe on BTypeImmediate
  // Probe on {BTypeImmediate[11], BTypeImmediate[9:4], ins[24:15], funct3}
  // Probe on {BTypeImmediate[11], BTypeImmediate[9:0], BTypeImmediate[10]}
  Multiplexer #(.Bits(5)) multiplexer_1 (
    .sel(control_1_jalr), .in_0(PC_p4), .in_1(register_file_1_data1_out[6:2]), .out(multiplexer_1_out));
  // Probe on add_1_c_o
  // Probe on {BTypeImmediate[11], BTypeImmediate[9:4], ins[24:15], funct3, BTypeImmediate[3:0], BTypeImmediate[10], ins[6:0]}
  Multiplexer #(.Bits(5)) multiplexer_2 (
    .sel(control_1_jalr), .in_0({BTypeImmediate[5:4], ins[24:22]}), .in_1({BTypeImmediate[5:4], ins[24:22]}),
    .out(multiplexer_2_out));
  Multiplexer #(.Bits(5)) multiplexer_3 (.sel(and_1_out), .in_0(add_1_s), .in_1(add_2_s), .out(PC_p1));
  Multiplexer #(.Bits(5)) multiplexer_4 (
    .sel(control_1_condbranch), .in_0(multiplexer_2_out), .in_1(BTypeImmediate[5:1]), .out(multiplexer_4_out));
  // Probe on multiplexer_4_out
  BitExtender #(.inputBits(12), .outputBits(32)) bitextender_1 (
    .in({BTypeImmediate[11], BTypeImmediate[9:4], ins[24:20]}), .out(bitextender_1_out));
  BitExtender #(.inputBits(12), .outputBits(32)) bitextender_2 (
    .in({BTypeImmediate[11], BTypeImmediate[9:0], BTypeImmediate[10]}), .out(bitextender_2_out));
  Add #(.Bits(5)) add_2 (.a(multiplexer_4_out), .b(multiplexer_1_out), .c_i(1'b0), .s(add_2_s));  // open: c_o
  control control_1 (
    .opcode(ins[6:0]), .ALUOp(control_1_aluop), .Jalr(control_1_jalr), .ALUSrc(control_1_alusrc),
    .MemtoReg(control_1_memtoreg), .RegWrite(control_1_regwrite), .MemRead(control_1_memread),
    .MemWrite(control_1_memwrite), .Branch(control_1_branch), .PCToReg(control_1_pctoreg),
    .CondBranch(control_1_condbranch), .UpperImm(control_1_upperimm));
  register_file register_file_1 (
    .clk(clk_t), .read_reg1(ins[19:15]), .read_reg2(ins[24:20]), .data_in(multiplexer_9_out),
    .write_reg({BTypeImmediate[3:0], BTypeImmediate[10]}), .str(control_1_regwrite),
    .data1_out(register_file_1_data1_out), .data2_out(register_file_1_data2_out));
  Multiplexer #(.Bits(32)) multiplexer_5 (
    .sel(control_1_memwrite), .in_0(bitextender_1_out), .in_1(bitextender_2_out), .out(multiplexer_5_out));
  // Probe on bitextender_1_out
  xor xor_1 (xor_1_out, funct3[2], alu_1_zero);
  Multiplexer #(.Bits(32)) multiplexer_6 (
    .sel(control_1_alusrc), .in_0(register_file_1_data2_out), .in_1(multiplexer_5_out),
    .out(multiplexer_6_out));
  or or_2 (or_2_out, not_1_out, xor_1_out);
  not not_1 (not_1_out, control_1_condbranch);
  alu alu_1 (
    .in_1(register_file_1_data1_out), .in_2(multiplexer_6_out), .operation(alu_control_1_op),
    .out(alu_1_out), .zero(alu_1_zero));
  alu_control alu_control_1 (.funct3(funct3), .i30(BTypeImmediate[9]), .ALUOp(control_1_aluop), .Op(alu_control_1_op));
  and and_1 (and_1_out, or_2_out, control_1_branch);
  RAMDualPort #(.AddrBits(4), .Bits(32)) ramdualport_1 (
    .A(alu_1_out[3:0]), .Din(register_file_1_data2_out), .str(control_1_memwrite), .C(clk_t),
    .ld(control_1_memread), .D(ramdualport_1_d));
  Multiplexer #(.Bits(32)) multiplexer_7 (
    .sel(not_2_out), .in_0(ramdualport_1_d), .in_1(alu_1_out), .out(multiplexer_7_out));
  not not_2 (not_2_out, control_1_memtoreg);
  Multiplexer #(.Bits(32)) multiplexer_8 (
    .sel(control_1_pctoreg), .in_0(multiplexer_7_out), .in_1({{25{1'b0}}, add_1_s, 2'b00}),
    .out(multiplexer_8_out));
  Multiplexer #(.Bits(32)) multiplexer_9 (
    .sel(control_1_upperimm), .in_0(multiplexer_8_out),
    .in_1({BTypeImmediate[11], BTypeImmediate[9:4], ins[24:15], funct3, {12{1'b0}}}), .out(multiplexer_9_out));

  // Other names for the same wires on the sheet: opcode[6:0] = ins[6:0];
  //   ins (some bits) = {BTypeImmediate[11], BTypeImmediate[9:4], funct3, BTypeImmediate[3:0], BTypeImmediate[10]};
  //   rd[4:0] = {BTypeImmediate[3:0], BTypeImmediate[10]};
  //   STypeImmediate[11:0] = {BTypeImmediate[11], BTypeImmediate[9:0], BTypeImmediate[10]};
  //   JTypeImmediate[20:1] = {BTypeImmediate[11], ins[19:15], funct3, ins[20], BTypeImmediate[9:4], ins[24:21]};
  //   UTypeImmediate[19:0] = {BTypeImmediate[11], BTypeImmediate[9:4], ins[24:15], funct3}; rs1[4:0] = ins[19:15];
  //   ITypeImmediate[11:0] = {BTypeImmediate[11], BTypeImmediate[9:4], ins[24:20]}; rs2[4:0] = ins[24:20];
  //   i30 = BTypeImmediate[9]

  // Notes on the sheet:
  //   clk: Hz: 5
  //   https://msyksphinz-self.github.io/riscv-isadoc/html/rvi.html#lb
  //   contents of rom_1 (hex, n*v repeats v):
  //   100093,100113,2000213,2081b3,10093,18113,fff20213,20463,fedff06f
  //   ,302023,ffdff06f
endmodule
