// Digital circuit register_file.dig as structural Verilog
module register_file (
  input  clk,
  input  [4:0] read_reg1,
  input  [4:0] read_reg2,
  input  [31:0] data_in,
  input  [4:0] write_reg,
  input  str,
  output [31:0] data1_out,
  output [31:0] data2_out
);

  wire demultiplexer_1_out_0, demultiplexer_1_out_1, demultiplexer_1_out_2, demultiplexer_1_out_3,
       demultiplexer_1_out_4, demultiplexer_1_out_5, demultiplexer_1_out_6, demultiplexer_1_out_7,
       demultiplexer_1_out_8, demultiplexer_1_out_9, demultiplexer_1_out_10, demultiplexer_1_out_11,
       demultiplexer_1_out_12, demultiplexer_1_out_13, demultiplexer_1_out_14, demultiplexer_1_out_15,
       demultiplexer_1_out_16, demultiplexer_1_out_17, demultiplexer_1_out_18, demultiplexer_1_out_19,
       demultiplexer_1_out_20, demultiplexer_1_out_21, demultiplexer_1_out_22, demultiplexer_1_out_23,
       demultiplexer_1_out_24, demultiplexer_1_out_25, demultiplexer_1_out_26, demultiplexer_1_out_27,
       demultiplexer_1_out_28, demultiplexer_1_out_29, demultiplexer_1_out_30, demultiplexer_1_out_31;
  wire [4:0] multiplexer_1_out;
  wire [31:0] x1_out, x2_out, x3_out, x4_out, x5_out, x6_out, x7_out, x8_out, x9_out, x10_out, x11_out,
       x12_out, x13_out, x14_out, x15_out, x16_out, x17_out, x18_out, x19_out, x20_out, x21_out, x22_out,
       x23_out, x24_out, x25_out, x26_out, x27_out, x28_out, x29_out, x30_out, x31_out;

  Multiplexer #(.Bits(5)) multiplexer_1 (.sel(str), .in_0({5{1'b0}}), .in_1(write_reg), .out(multiplexer_1_out));
  Demultiplexer #(.Selector_Bits(5)) demultiplexer_1 (
    .sel(multiplexer_1_out), .in(1'b1), .out_0(demultiplexer_1_out_0), .out_1(demultiplexer_1_out_1),
    .out_2(demultiplexer_1_out_2), .out_3(demultiplexer_1_out_3), .out_4(demultiplexer_1_out_4),
    .out_5(demultiplexer_1_out_5), .out_6(demultiplexer_1_out_6), .out_7(demultiplexer_1_out_7),
    .out_8(demultiplexer_1_out_8), .out_9(demultiplexer_1_out_9), .out_10(demultiplexer_1_out_10),
    .out_11(demultiplexer_1_out_11), .out_12(demultiplexer_1_out_12), .out_13(demultiplexer_1_out_13),
    .out_14(demultiplexer_1_out_14), .out_15(demultiplexer_1_out_15), .out_16(demultiplexer_1_out_16),
    .out_17(demultiplexer_1_out_17), .out_18(demultiplexer_1_out_18), .out_19(demultiplexer_1_out_19),
    .out_20(demultiplexer_1_out_20), .out_21(demultiplexer_1_out_21), .out_22(demultiplexer_1_out_22),
    .out_23(demultiplexer_1_out_23), .out_24(demultiplexer_1_out_24), .out_25(demultiplexer_1_out_25),
    .out_26(demultiplexer_1_out_26), .out_27(demultiplexer_1_out_27), .out_28(demultiplexer_1_out_28),
    .out_29(demultiplexer_1_out_29), .out_30(demultiplexer_1_out_30), .out_31(demultiplexer_1_out_31));
  // Probe on demultiplexer_1_out_0
  Register #(.Bits(32), .isProgramCounter("true")) x1 (.D(data_in), .C(clk), .en(demultiplexer_1_out_1), .Q(x1_out));
  Register #(.Bits(32), .isProgramCounter("true")) x2 (.D(data_in), .C(clk), .en(demultiplexer_1_out_2), .Q(x2_out));
  Register #(.Bits(32), .isProgramCounter("true")) x3 (.D(data_in), .C(clk), .en(demultiplexer_1_out_3), .Q(x3_out));
  Register #(.Bits(32), .isProgramCounter("true")) x4 (.D(data_in), .C(clk), .en(demultiplexer_1_out_4), .Q(x4_out));
  Register #(.Bits(32), .isProgramCounter("true")) x5 (.D(data_in), .C(clk), .en(demultiplexer_1_out_5), .Q(x5_out));
  Register #(.Bits(32), .isProgramCounter("true")) x6 (.D(data_in), .C(clk), .en(demultiplexer_1_out_6), .Q(x6_out));
  Register #(.Bits(32), .isProgramCounter("true")) x7 (.D(data_in), .C(clk), .en(demultiplexer_1_out_7), .Q(x7_out));
  Register #(.Bits(32), .isProgramCounter("true")) x8 (.D(data_in), .C(clk), .en(demultiplexer_1_out_8), .Q(x8_out));
  Register #(.Bits(32), .isProgramCounter("true")) x9 (.D(data_in), .C(clk), .en(demultiplexer_1_out_9), .Q(x9_out));
  Register #(.Bits(32), .isProgramCounter("true")) x10 (.D(data_in), .C(clk), .en(demultiplexer_1_out_10), .Q(x10_out));
  Register #(.Bits(32), .isProgramCounter("true")) x11 (.D(data_in), .C(clk), .en(demultiplexer_1_out_11), .Q(x11_out));
  Register #(.Bits(32), .isProgramCounter("true")) x12 (.D(data_in), .C(clk), .en(demultiplexer_1_out_12), .Q(x12_out));
  Register #(.Bits(32), .isProgramCounter("true")) x13 (.D(data_in), .C(clk), .en(demultiplexer_1_out_13), .Q(x13_out));
  Register #(.Bits(32), .isProgramCounter("true")) x14 (.D(data_in), .C(clk), .en(demultiplexer_1_out_14), .Q(x14_out));
  Register #(.Bits(32), .isProgramCounter("true")) x15 (.D(data_in), .C(clk), .en(demultiplexer_1_out_15), .Q(x15_out));
  Register #(.Bits(32), .isProgramCounter("true")) x16 (.D(data_in), .C(clk), .en(demultiplexer_1_out_16), .Q(x16_out));
  Register #(.Bits(32), .isProgramCounter("true")) x17 (.D(data_in), .C(clk), .en(demultiplexer_1_out_17), .Q(x17_out));
  Register #(.Bits(32), .isProgramCounter("true")) x18 (.D(data_in), .C(clk), .en(demultiplexer_1_out_18), .Q(x18_out));
  Register #(.Bits(32), .isProgramCounter("true")) x19 (.D(data_in), .C(clk), .en(demultiplexer_1_out_19), .Q(x19_out));
  Register #(.Bits(32), .isProgramCounter("true")) x20 (.D(data_in), .C(clk), .en(demultiplexer_1_out_20), .Q(x20_out));
  Register #(.Bits(32), .isProgramCounter("true")) x21 (.D(data_in), .C(clk), .en(demultiplexer_1_out_21), .Q(x21_out));
  Register #(.Bits(32), .isProgramCounter("true")) x22 (.D(data_in), .C(clk), .en(demultiplexer_1_out_22), .Q(x22_out));
  Register #(.Bits(32), .isProgramCounter("true")) x23 (.D(data_in), .C(clk), .en(demultiplexer_1_out_23), .Q(x23_out));
  Register #(.Bits(32), .isProgramCounter("true")) x24 (.D(data_in), .C(clk), .en(demultiplexer_1_out_24), .Q(x24_out));
  Register #(.Bits(32), .isProgramCounter("true")) x25 (.D(data_in), .C(clk), .en(demultiplexer_1_out_25), .Q(x25_out));
  Register #(.Bits(32), .isProgramCounter("true")) x26 (.D(data_in), .C(clk), .en(demultiplexer_1_out_26), .Q(x26_out));
  Register #(.Bits(32), .isProgramCounter("true")) x27 (.D(data_in), .C(clk), .en(demultiplexer_1_out_27), .Q(x27_out));
  Register #(.Bits(32), .isProgramCounter("true")) x28 (.D(data_in), .C(clk), .en(demultiplexer_1_out_28), .Q(x28_out));
  Register #(.Bits(32), .isProgramCounter("true")) x29 (.D(data_in), .C(clk), .en(demultiplexer_1_out_29), .Q(x29_out));
  Register #(.Bits(32), .isProgramCounter("true")) x30 (.D(data_in), .C(clk), .en(demultiplexer_1_out_30), .Q(x30_out));
  Register #(.Bits(32), .isProgramCounter("true")) x31 (.D(data_in), .C(clk), .en(demultiplexer_1_out_31), .Q(x31_out));
  Multiplexer #(.Selector_Bits(5), .Bits(32)) multiplexer_2 (
    .sel(read_reg1), .in_0({32{1'b0}}), .in_1(x1_out), .in_2(x2_out), .in_3(x3_out), .in_4(x4_out),
    .in_5(x5_out), .in_6(x6_out), .in_7(x7_out), .in_8(x8_out), .in_9(x9_out), .in_10(x10_out),
    .in_11(x11_out), .in_12(x12_out), .in_13(x13_out), .in_14(x14_out), .in_15(x15_out), .in_16(x16_out),
    .in_17(x17_out), .in_18(x18_out), .in_19(x19_out), .in_20(x20_out), .in_21(x21_out), .in_22(x22_out),
    .in_23(x23_out), .in_24(x24_out), .in_25(x25_out), .in_26(x26_out), .in_27(x27_out), .in_28(x28_out),
    .in_29(x29_out), .in_30(x30_out), .in_31(x31_out), .out(data1_out));
  Multiplexer #(.Selector_Bits(5), .Bits(32)) multiplexer_3 (
    .sel(read_reg2), .in_0({32{1'b0}}), .in_1(x1_out), .in_2(x2_out), .in_3(x3_out), .in_4(x4_out),
    .in_5(x5_out), .in_6(x6_out), .in_7(x7_out), .in_8(x8_out), .in_9(x9_out), .in_10(x10_out),
    .in_11(x11_out), .in_12(x12_out), .in_13(x13_out), .in_14(x14_out), .in_15(x15_out), .in_16(x16_out),
    .in_17(x17_out), .in_18(x18_out), .in_19(x19_out), .in_20(x20_out), .in_21(x21_out), .in_22(x22_out),
    .in_23(x23_out), .in_24(x24_out), .in_25(x25_out), .in_26(x26_out), .in_27(x27_out), .in_28(x28_out),
    .in_29(x29_out), .in_30(x30_out), .in_31(x31_out), .out(data2_out));

  // Other names for the same wires on the sheet: write_data[31:0] = data_in

  // Notes on the sheet:
  //   data_in: data to write to selected register
  //   str: store/write enable
endmodule
