// Digital circuit display_test.dig as structural Verilog
module display_test (
  input  [7:0] addr,
  input  clk,
  input  [4:0] data,
  input  store,
  input  load,
  input  [7:0] addr_2,
  input  clk_2,
  input  [7:0] data_2,
  input  store_2,
  input  load_2,
  input  [9:0] addr_3,
  input  clk_3,
  input  [7:0] data_3,
  input  store_3,
  input  load_3
);

  wire test1_p6, test2_p6, test3_p6;

  // ZenohRAMDualPort #(.AddrBits(8), .Bits(5), .zenohKeyExpr("test1")) test1: pin names not known; wires that end beside it: addr, data, store, clk, load, test1_p6
  // ZenohRAMDualPort #(.AddrBits(8), .zenohKeyExpr("test2"), .Bits(8)) test2: pin names not known; wires that end beside it: addr_2, data_2, store_2, clk_2, load_2, test2_p6
  // ZenohRAMDualPort #(.AddrBits(10), .zenohKeyExpr("test3"), .Bits(8)) test3: pin names not known; wires that end beside it: addr_3, data_3, store_3, clk_3, load_3, test3_p6
  // Probe on test1_p6
  // Probe on test2_p6
  // Probe on test3_p6

  // Notes on the sheet:
  //   clk: Hz: 5000
  //   load: default 1
  //   clk_2: Hz: 5000
  //   load_2: default 1
  //   clk_3: Hz: 5000
  //   load_3: default 1
  //   monochrome
  //   5 bit word
  //   8 bit addr
  //   shading
  //   8 bit word
  //   8 bit addr
  //   16 x 16 display
  //   rgba8
  //   8 bit word
  //   8 bit addr
  //   16 x 16 display
endmodule
