// Digital circuit acceptance_test_key.dig as structural Verilog
module acceptance_test_key (
  input  clk,
  input  in_2,
  input  [3:0] in_3,
  input  [7:0] in_4,
  input  in_5
);

  wire or_1_out, or_2_out, zenohsubscriber_1_p1, zenohsubscriber_2_p1;
  wire [3:0] zenohregister_1_p4;
  wire [4:0] bitextender_1_out;
  wire [7:0] multiplexer_1_out, zenohramdualport_1_p6, zenohregister_2_p4;

  Multiplexer #(.Bits(8)) multiplexer_1 (
    .sel(or_2_out), .in_0(in_4), .in_1(zenohramdualport_1_p6), .out(multiplexer_1_out));
  // ZenohSubscriber #(.zenohKeyExpr("store")) zenohsubscriber_1: pin names not known; wires that end beside it: zenohsubscriber_1_p1
  // ZenohSubscriber #(.zenohKeyExpr("load")) zenohsubscriber_2: pin names not known; wires that end beside it: zenohsubscriber_2_p1
  // ZenohRegister #(.zenohKeyExpr("addr"), .Bits(4)) zenohregister_1: pin names not known; wires that end beside it: in_3, clk, 1'b1, zenohregister_1_p4
  // ZenohRegister #(.zenohKeyExpr("data"), .Bits(8)) zenohregister_2: pin names not known; wires that end beside it: multiplexer_1_out, clk, 1'b1, zenohregister_2_p4
  or or_1 (or_1_out, in_2, zenohsubscriber_1_p1);
  or or_2 (or_2_out, in_5, zenohsubscriber_2_p1);
  // ZenohRAMDualPort #(.AddrBits(4), .zenohKeyExpr("mem"), .Bits(8)) zenohramdualport_1: pin names not known; wires that end beside it: zenohregister_1_p4, zenohregister_2_p4, or_1_out, clk, 1'b1, zenohramdualport_1_p6
  BitExtender #(.inputBits(4), .outputBits(5)) bitextender_1 (.in(zenohregister_1_p4), .out(bitextender_1_out));
  GraphicCard #(.graphicHeight(4), .graphicWidth(4), .Bits(8)) graphiccard_1 (
    .A(bitextender_1_out), .str(or_1_out), .C(clk), .ld(1'b0), .B(1'b0), .D(zenohregister_2_p4));
  // ZenohPublisher #(.zenohKeyExpr("mem_out"), .Bits(8)) zenohpublisher_1: pin names not known; wires that end beside it: zenohramdualport_1_p6

  // Notes on the sheet:
  //   clk: Hz: 20
endmodule
