// Digital circuit zenoh_pub_test.dig as structural Verilog
module zenoh_pub_test (
  input  clk
);

  // ZenohPublisher #(.zenohKeyExpr("host/blahblahblah")) a_zenoh_test: pin names not known; wires that end beside it: clk
  // ZenohPublisher #(.zenohKeyExpr("host/blahblahblah2")) a_zenoh_test2: pin names not known; wires that end beside it: clk

  // Notes on the sheet:
  //   clk: Hz: 5
endmodule
