// Digital circuit zenoh_ram_dual_access_test.dig as structural Verilog
module zenoh_ram_dual_access_test (
  input  [2:0] in_1,
  input  [3:0] in_2,
  input  [2:0] in_3,
  input  in_4,
  input  in_5,
  input  clk
);

  wire zenohramdualaccess_1_p7, zenohramdualaccess_1_p8;

  // ZenohRAMDualAccess #(.AddrBits(3), .Bits(4), .zenohKeyExpr("test_ram")) zenohramdualaccess_1: pin names not known; wires that end beside it: in_5, clk, in_4, in_1, in_2, in_3, zenohramdualaccess_1_p7, zenohramdualaccess_1_p8
  // Probe on zenohramdualaccess_1_p7
  // Probe on zenohramdualaccess_1_p8
endmodule
