// Digital circuit zenoh_ram_test.dig as structural Verilog
module zenoh_ram_test (
  input  [1:0] in_1,
  input  [9:0] in_2,
  input  in_3,
  input  in_4,
  input  in_5,
  input  in_7,
  output [9:0] out_6
);

  // ZenohPublisher #(.zenohKeyExpr("test2/test")) zenohpublisher_1: pin names not known; wires that end beside it: in_7
  // ZenohRAMDualPort #(.zenohKeyExpr("test_ram"), .Bits(10)) zenohramdualport_1: pin names not known; wires that end beside it: in_1, in_2, in_3, in_4, in_5, out_6
endmodule
