// Digital circuit zenoh_simple.dig as structural Verilog
module zenoh_simple (
);

  wire zenohsubscriber_1_p1, zenohsubscriber_2_p1;

  // ZenohSubscriber #(.zenohKeyExpr("test")) zenohsubscriber_1: pin names not known; wires that end beside it: zenohsubscriber_1_p1
  // ZenohPublisher #(.zenohKeyExpr("test2")) zenohpublisher_1: pin names not known; wires that end beside it: zenohsubscriber_1_p1
  // ZenohSubscriber #(.zenohKeyExpr("test2")) zenohsubscriber_2: pin names not known; wires that end beside it: zenohsubscriber_2_p1
  LED led_1 (.in(zenohsubscriber_2_p1));
endmodule
