// Digital circuit zenoh_test.dig as structural Verilog
module zenoh_test (
  input  clk
);

  wire add_1_c_o, not_1_out, register_2_q, zenohsubscriber_1_p1;
  wire [2:0] add_1_s, barrelshifter_1_out, register_1_q;

  // ZenohSubscriber #(.Bits(2), .zenohKeyExpr("zenoh_test/clock/speed")) zenohsubscriber_1: pin names not known; wires that end beside it: zenohsubscriber_1_p1
  BarrelShifter #(.Bits(3)) barrelshifter_1 (.in(3'b001), .shift(zenohsubscriber_1_p1), .out(barrelshifter_1_out));
  Register #(.Bits(3)) register_1 (.D(add_1_s), .C(clk), .en(1'b1), .Q(register_1_q));
  Add #(.Bits(3)) add_1 (.a(barrelshifter_1_out), .b(register_1_q), .c_i(1'b0), .s(add_1_s), .c_o(add_1_c_o));
  // ZenohPublisher #(.zenohKeyExpr("zenoh_test/real_clock_value")) clock_value: pin names not known; wires that end beside it: clk, clk
  // ZenohPublisher #(.zenohKeyExpr("zenoh_test/clock/counter"), .Bits(3)) counter: pin names not known; wires that end beside it: register_1_q
  Register register_2 (.D(not_1_out), .C(add_1_c_o), .en(add_1_c_o), .Q(register_2_q));
  not not_1 (not_1_out, register_2_q);
  // ZenohPublisher #(.zenohKeyExpr("zenoh_test/clock/value")) simulated_clock: pin names not known; wires that end beside it: register_2_q

  // Notes on the sheet:
  //   clk: Hz: 2
endmodule
